# Fritzing sketch stoply (saved by Fritzing 1.0.2b)
breadboards: 4

parts:
  Part1 = Arduino Uno (Rev3)
  LED4 = LED - 5mm [color="Green (555nm)" current=0.030A package="5 mm [THT]"]
  LED5 = LED - 5mm [color="Yellow (585nm)" current=0.030A package="5 mm [THT]"]
  LED6 = LED - 5mm [color="Red (633nm)" current=0.030A package="5 mm [THT]"]
  R2 = Resistor [tolerance=±5% power=0.25W resistance=220 package=THT]
  LED7 = LED - 5mm [color="Red (633nm)" current=0.030A package="5 mm [THT]"]
  R3 = Resistor [tolerance=±5% power=0.25W resistance=220 package=THT]
  LED8 = LED - 5mm [color="Yellow (585nm)" current=0.030A package="5 mm [THT]"]
  LED9 = LED - 5mm [color="Green (555nm)" current=0.030A package="5 mm [THT]"]
  LED10 = LED - 5mm [color="Green (555nm)" current=0.030A package="5 mm [THT]"]
  LED11 = LED - 5mm [color="Yellow (585nm)" current=0.030A package="5 mm [THT]"]
  LED12 = LED - 5mm [color="Red (633nm)" current=0.030A package="5 mm [THT]"]
  R4 = Resistor [tolerance=±5% power=0.25W resistance=220 package=THT]
  LED13 = LED - 5mm [color="Green (555nm)" current=0.030A package="5 mm [THT]"]
  LED14 = LED - 5mm [color="Yellow (585nm)" current=0.030A package="5 mm [THT]"]
  LED15 = LED - 5mm [color="Red (633nm)" current=0.030A package="5 mm [THT]"]
  R5 = Resistor [tolerance=±5% power=0.25W resistance=220 package=THT]

nets:
  N1: Part1.D8, LED6.anode, LED15.anode
  N2: Part1.D9_PWM, LED5.anode, LED14.anode
  N3: Part1.D10_PWM/SS, LED4.anode, LED13.anode
  N4: Part1.D11_PWM/MOSI, LED9.anode, LED10.anode
  N5: Part1.D12/MISO, LED8.anode, LED11.anode
  N6: Part1.D13/SCK, LED7.anode, LED12.anode
  N7: Part1.GND, R2.Pin_0, R3.Pin_0, R4.Pin_0
  N8: LED4.cathode, LED5.cathode, LED6.cathode, R2.Pin_1
  N9: LED7.cathode, R3.Pin_1, LED8.cathode, LED9.cathode
  N10: LED10.cathode, LED11.cathode, LED12.cathode, R4.Pin_1
  N11: LED13.cathode, LED14.cathode, LED15.cathode, R5.Pin_1
